# Fritzing sketch wiring (saved by Fritzing 1.0.3b)
breadboards: 1

parts:
  U1 = ESP32-38PinWide [part_number=ESP32-38PinWide]
  U2 = RF-LINK_RX [package=rf-link_rx]
  S1 = Pushbutton [package="[THT]"]
  LED1 = smd LED [color="Blue (430nm)" package="1206 [SMD]"]
  R1 = Resistor [tolerance=±5% resistance=10 package="0402 [SMD]"]

nets:
  N1: U1.3.3, U2.+5V
  N2: U1.GPIO32, U2.DATA
  N3: U1.GPIO26, LED1.anode
  N4: U1.GPIO27, S1.Pin_3, S1.Pin_4
  GND: U1.GND, U2.GND, S1.Pin_1, S1.Pin_2, R1.Pin_0
  N5: LED1.cathode, R1.Pin_1

custom parts:
  ESP32-38PinWide: Generic 38-Pin ESP32 with wide format (only access to one side of pins on a breadboard) based on Stephen Lilley's HiLetgo ESP-WROOM-32 ESP32 ESP-32S Development Board.
